# Fritzing sketch thermodisplay (saved by Fritzing 0.9.2b)
breadboards: 1

parts:
  U1 = atmega328 [package=dip]
  RHT1 = Humidity and Temperature Sensor RHT03
  J1 = Power Jack [package=power_jack_combo]
  U2 = Voltage Regulator - 5V [package="TO220 [THT]"]
  C1 = Ceramic Capacitor [capacitance=100nF package="100 mil [THT, multilayer]"]
  Grove1 = Grove OLED 128x96
  R1 = Resistor [tolerance=±5% resistance=10k package="0603 [SMD]"]
  C2 = Capacitor [package=cap-pth-small2]

nets:
  N1: U1.D2, RHT1.Data-signal, R1.Pin_1
  VCC: U1.VCC, RHT1.Vcc, Grove1.VCC, R1.Pin_0, C2.1
  N2: U1.GND#7, RHT1.GND_1, Grove1.GND, C2.2
  N3: U1.A4, Grove1.SDA
  N4: U1.A5, Grove1.SCL
  N5: J1.GNDBREAK, U2.GND, C1.1
  N6: J1.PWR, U2.input_voltage
  N7: U2.output_voltage, C1.0
